// Logisim project Hamming_à_compléter.circ as structural Verilog: 7 circuits, main circuit main
module main (
  input  [3:0] \données ,
  input  [6:0] \mot_reçu ,
  output [6:0] \mot_décodé ,
  output [6:0] mot_de_code_de_Hamming_7_4,
  output \zéro_erreur 
);

  wire [2:0] xor3_3_1_c2c1c0_avec_ci_ai_xor_bi, xor3_4_a2_xor_a1_xor_a0;
  wire [6:0] dec3renv_1_seul_le_bit_en_position__a2a1a0__2_vaut_1;

  xor3 xor3_1 (.a2a1a0({\données [0], \données [1], \données [2]}), .a2_xor_a1_xor_a0(mot_de_code_de_Hamming_7_4[3]));
  xor3 xor3_2 (.a2a1a0({\données [0], \données [1], \données [3]}), .a2_xor_a1_xor_a0(mot_de_code_de_Hamming_7_4[5]));
  xor3 xor3_3 (.a2a1a0({\données [0], \données [2], \données [3]}), .a2_xor_a1_xor_a0(mot_de_code_de_Hamming_7_4[6]));
  xor3 xor3_4 (.a2a1a0({\mot_reçu [0], \mot_reçu [1], \mot_reçu [2]}), .a2_xor_a1_xor_a0(xor3_4_a2_xor_a1_xor_a0[0]));
  xor3 xor3_5 (.a2a1a0({\mot_reçu [0], \mot_reçu [1], \mot_reçu [4]}), .a2_xor_a1_xor_a0(xor3_4_a2_xor_a1_xor_a0[1]));
  xor3 xor3_6 (.a2a1a0({\mot_reçu [0], \mot_reçu [2], \mot_reçu [4]}), .a2_xor_a1_xor_a0(xor3_4_a2_xor_a1_xor_a0[2]));
  xor3_3 xor3_3_1 (
    .a2a1a0({\mot_reçu [6:5], \mot_reçu [3]}), .b2b1b0(xor3_4_a2_xor_a1_xor_a0),
    .c2c1c0_avec_ci_ai_xor_bi(xor3_3_1_c2c1c0_avec_ci_ai_xor_bi));
  dec3renv dec3renv_1 (
    .a2a1a0(xor3_3_1_c2c1c0_avec_ci_ai_xor_bi),
    .seul_le_bit_en_position__a2a1a0__2_vaut_1({\zéro_erreur , dec3renv_1_seul_le_bit_en_position__a2a1a0__2_vaut_1}));
  xor7_7 xor7_7_1 (
    .a6__a0(\mot_reçu ), .b6__b0(dec3renv_1_seul_le_bit_en_position__a2a1a0__2_vaut_1),
    .c6__c0_avec_ci_ai_xor_bi(\mot_décodé ));

  assign {mot_de_code_de_Hamming_7_4[4], mot_de_code_de_Hamming_7_4[2:0]} = \données ;

  // Notes on the sheet:
  //   1234567
  //   3567
  //   1234567
  //   1234567
endmodule

module dec3 (
  input  [2:0] a2a1a0,
  output [7:0] seul_le_bit_en_position__a2a1a0__2_vaut_1
);

  and s7 (seul_le_bit_en_position__a2a1a0__2_vaut_1[7], a2a1a0[2], a2a1a0[1], a2a1a0[0]);
  and s6 (seul_le_bit_en_position__a2a1a0__2_vaut_1[6], a2a1a0[2], a2a1a0[1], ~a2a1a0[0]);  // AND_Gate
  and s5 (seul_le_bit_en_position__a2a1a0__2_vaut_1[5], a2a1a0[2], ~a2a1a0[1], a2a1a0[0]);  // AND_Gate
  and s3 (seul_le_bit_en_position__a2a1a0__2_vaut_1[3], ~a2a1a0[2], a2a1a0[1], a2a1a0[0]);  // AND_Gate
  and s4 (seul_le_bit_en_position__a2a1a0__2_vaut_1[4], a2a1a0[2], ~a2a1a0[1], ~a2a1a0[0]);  // AND_Gate
  and s2 (seul_le_bit_en_position__a2a1a0__2_vaut_1[2], ~a2a1a0[2], a2a1a0[1], ~a2a1a0[0]);  // AND_Gate
  and s1 (seul_le_bit_en_position__a2a1a0__2_vaut_1[1], ~a2a1a0[2], ~a2a1a0[1], a2a1a0[0]);  // AND_Gate
  and s0 (seul_le_bit_en_position__a2a1a0__2_vaut_1[0], ~a2a1a0[2], ~a2a1a0[1], ~a2a1a0[0]);  // AND_Gate

  // Notes on the sheet:
  //   dec3: décodeur 3 bits (classique: position 0 à droite)
endmodule

// ced3
module dec3renv (
  input  [2:0] a2a1a0,
  output [7:0] seul_le_bit_en_position__a2a1a0__2_vaut_1
);

  // AND_Gate s0 has open pins: out=seul_le_bit_en_position__a2a1a0__2_vaut_1[7]
  // AND_Gate s1 has open pins: out=seul_le_bit_en_position__a2a1a0__2_vaut_1[6]
  // AND_Gate s2 has open pins: out=seul_le_bit_en_position__a2a1a0__2_vaut_1[5]
  // AND_Gate s4 has open pins: out=seul_le_bit_en_position__a2a1a0__2_vaut_1[3]
  // AND_Gate s3 has open pins: out=seul_le_bit_en_position__a2a1a0__2_vaut_1[4]
  // AND_Gate s6 has open pins: out=seul_le_bit_en_position__a2a1a0__2_vaut_1[1]
  // AND_Gate s5 has open pins: out=seul_le_bit_en_position__a2a1a0__2_vaut_1[2]
  // AND_Gate s7 has open pins: out=seul_le_bit_en_position__a2a1a0__2_vaut_1[0]

  // Notes on the sheet:
  //   sur le modèle du décodeur dec3, terminer le câblage
  //   de ce décodeur 3 bits renversé (position 0 à gauche)
endmodule

module xor3 (
  input  [2:0] a2a1a0,
  output a2_xor_a1_xor_a0
);

  wire xor_1_out;

  xor xor_1 (xor_1_out, a2a1a0[0], a2a1a0[1]);
  xor xor_2 (a2_xor_a1_xor_a0, xor_1_out, a2a1a0[2]);
endmodule

// x33
module xor3_3 (
  input  [2:0] a2a1a0,
  input  [2:0] b2b1b0,
  output [2:0] c2c1c0_avec_ci_ai_xor_bi
);


  // Notes on the sheet:
  //   à terminer...
endmodule

// x77
module xor7_7 (
  input  [6:0] a6__a0,
  input  [6:0] b6__b0,
  output [6:0] c6__c0_avec_ci_ai_xor_bi
);


  // Notes on the sheet:
  //   à terminer...
  //   plusieurs options ici:
  //   - changer les trois splitters donnés et câbler fil à fil 
  //   - utiliser une porte xor et deux modules x3+3
  //   - repartir de x3+3, et continuer en cascade x4+4, etc
endmodule

module xor_et_cie (
  input  a1,
  input  a1_2,
  input  a2,
  input  a2_2,
  input  a1_3,
  input  a1_4,
  input  a2_3,
  input  a2_4,
  input  a3,
  input  a3_2,
  input  a1_5,
  input  a1_6,
  input  a2_5,
  input  a2_6,
  input  a3_3,
  input  a3_4,
  output a1_et_a2,
  output a1_xor_a2,
  output a1_et_a2_et_a3,
  output \_1_ssi_exactement_1_entrée_vaut_1 ,
  output a1_et_a2_et_a3_2,
  output a1_xor_a2_xor_a3
);

  wire and_3_out, xor_3_out;

  and and_1 (a1_et_a2, a1, a2);
  and and_2 (a1_et_a2_et_a3, a1_3, a2_3, a3);
  and and_3 (and_3_out, a1_5, a2_5);
  and and_4 (a1_et_a2_et_a3_2, and_3_out, a3_3);
  xor xor_1 (a1_xor_a2, a1_2, a2_2);
  ExactlyOne xor_2 (.out(\_1_ssi_exactement_1_entrée_vaut_1 ), .in0(a1_4), .in1(a2_4), .in2(a3_2));
  xor xor_3 (xor_3_out, a1_6, a2_6);
  xor xor_4 (a1_xor_a2_xor_a3, xor_3_out, a3_4);

  // Notes on the sheet:
  //   version intégrée
  //   I
  //   équivalentes
  //   I
  //   version cascade
  //   version intégrée
  //   !! calcule une "exclusion mutuelle" !!
  //   I
  //   non-équivalentes
  //   I
  //   version cascade
  //   c'est cette version cascade qui nous intéresse aujourd'hui: xor3
endmodule
