// Logisim project DM-CodeGray_Charly-Martin.circ as structural Verilog: 6 circuits, main circuit main
module main (
  input  [3:0] in_1,
  output [3:0] out_2
);

  INCGray incgray_1 (.in_1(in_1), .out_2(out_2));
endmodule

module INCGray (
  input  [3:0] in_1,
  output [3:0] out_2
);

  b_0 b_0_1 (.in_1(in_1), .out_2(out_2[0]));
  b_1 b_1_1 (.in_1(in_1), .out_2(out_2[1]));
  b_2 b_2_1 (.in_1(in_1), .out_2(out_2[2]));
  b_3 b_3_1 (.in_1(in_1), .out_2(out_2[3]));
endmodule

module b_3 (
  input  [3:0] in_1,
  output out_2
);

  wire and_1_out, and_2_out, and_3_out, and_4_out, and_5_out, and_6_out, and_7_out, and_8_out, not_1_out,
       not_2_out, not_3_out, not_4_out;

  not not_1 (not_1_out, in_1[3]);
  not not_2 (not_2_out, in_1[2]);
  not not_3 (not_3_out, in_1[1]);
  not not_4 (not_4_out, in_1[0]);
  and and_1 (and_1_out, not_1_out, in_1[2], not_3_out, not_4_out);
  and and_2 (and_2_out, in_1[3], not_2_out, not_3_out, in_1[0]);
  and and_3 (and_3_out, in_1[3], not_2_out, in_1[1], not_4_out);
  and and_4 (and_4_out, in_1[3], not_2_out, in_1[1], in_1[0]);
  and and_5 (and_5_out, in_1[3], in_1[2], not_3_out, not_4_out);
  and and_6 (and_6_out, in_1[3], in_1[2], not_3_out, in_1[0]);
  and and_7 (and_7_out, in_1[3], in_1[2], in_1[1], not_4_out);
  and and_8 (and_8_out, in_1[3], in_1[2], in_1[1], in_1[0]);
  or or_1 (out_2, and_1_out, and_2_out, and_3_out, and_4_out, and_5_out, and_6_out, and_7_out, and_8_out);
endmodule

module b_2 (
  input  [3:0] in_1,
  output out_2
);

  wire and_1_out, and_2_out, and_3_out, and_4_out, and_5_out, and_6_out, and_7_out, and_8_out, not_1_out,
       not_2_out, not_3_out, not_4_out;

  not not_1 (not_1_out, in_1[3]);
  not not_2 (not_2_out, in_1[1]);
  not not_3 (not_3_out, in_1[2]);
  not not_4 (not_4_out, in_1[0]);
  and and_1 (and_1_out, not_1_out, not_3_out, in_1[1], not_4_out);
  and and_2 (and_2_out, not_1_out, in_1[2], not_2_out, not_4_out);
  and and_3 (and_3_out, not_1_out, in_1[2], not_2_out, in_1[0]);
  and and_4 (and_4_out, not_1_out, in_1[2], in_1[1], not_4_out);
  and and_5 (and_5_out, not_1_out, in_1[2], in_1[1], in_1[0]);
  and and_6 (and_6_out, in_1[3], in_1[2], not_2_out, not_4_out);
  and and_7 (and_7_out, in_1[3], in_1[2], not_2_out, in_1[0]);
  and and_8 (and_8_out, in_1[3], in_1[2], in_1[1], in_1[0]);
  or or_1 (out_2, and_1_out, and_2_out, and_3_out, and_4_out, and_5_out, and_6_out, and_7_out, and_8_out);
endmodule

module b_1 (
  input  [3:0] in_1,
  output out_2
);

  wire and_1_out, and_2_out, and_3_out, and_4_out, and_5_out, and_6_out, and_7_out, and_8_out, not_1_out,
       not_2_out, not_3_out, not_4_out;

  not not_1 (not_1_out, in_1[3]);
  not not_2 (not_2_out, in_1[2]);
  not not_3 (not_3_out, in_1[1]);
  not not_4 (not_4_out, in_1[0]);
  and and_1 (and_1_out, not_1_out, not_2_out, not_3_out, in_1[0]);
  and and_2 (and_2_out, not_1_out, not_2_out, in_1[1], not_4_out);
  and and_3 (and_3_out, not_1_out, not_2_out, in_1[1], in_1[0]);
  and and_4 (and_4_out, not_1_out, in_1[2], in_1[1], not_4_out);
  and and_5 (and_5_out, in_1[3], not_2_out, in_1[1], not_4_out);
  and and_6 (and_6_out, in_1[3], in_1[2], not_3_out, in_1[0]);
  and and_7 (and_7_out, in_1[3], in_1[2], in_1[1], not_4_out);
  and and_8 (and_8_out, in_1[3], in_1[2], in_1[1], in_1[0]);
  or or_1 (out_2, and_1_out, and_2_out, and_3_out, and_4_out, and_5_out, and_6_out, and_7_out, and_8_out);
endmodule

module b_0 (
  input  [3:0] in_1,
  output out_2
);

  wire and_1_out, and_2_out, and_3_out, and_4_out, and_5_out, and_6_out, and_7_out, and_8_out, not_1_out,
       not_2_out, not_3_out, not_4_out;

  not not_1 (not_1_out, in_1[3]);
  not not_2 (not_2_out, in_1[1]);
  not not_3 (not_3_out, in_1[2]);
  not not_4 (not_4_out, in_1[0]);
  and and_1 (and_1_out, not_1_out, not_3_out, not_2_out, not_4_out);
  and and_2 (and_2_out, not_1_out, not_3_out, not_2_out, in_1[0]);
  and and_3 (and_3_out, not_1_out, in_1[2], in_1[1], not_4_out);
  and and_4 (and_4_out, not_1_out, in_1[2], in_1[1], in_1[0]);
  and and_5 (and_5_out, in_1[3], not_3_out, in_1[1], not_4_out);
  and and_6 (and_6_out, in_1[3], not_3_out, in_1[1], in_1[0]);
  and and_7 (and_7_out, in_1[3], in_1[2], not_2_out, not_4_out);
  and and_8 (and_8_out, in_1[3], in_1[2], not_2_out, in_1[0]);
  or or_1 (out_2, and_1_out, and_2_out, and_3_out, and_4_out, and_5_out, and_6_out, and_7_out, and_8_out);
endmodule
