// Logisim project DM_Charly_Martin.circ as structural Verilog: 4 circuits, main circuit main
module main (
  input  a,
  input  b,
  input  a_2,
  input  a_3,
  input  b_2,
  output a_b,
  output na,
  output a__b,
  output a_b_2
);

  wire cmp1_1_out_3, cmp1_1_out_4;

  EQ1 eq1_1 (.in_1(a), .out_3(a_b), .in_2(b));
  NOT not_1 (.in_1(a_2), .out_2(na));
  NOT not_2 (.in_1(cmp1_1_out_3), .out_2(a__b));
  CMP1 cmp1_1 (.in_1(a_3), .out_3(cmp1_1_out_3), .in_2(b_2), .out_4(cmp1_1_out_4));
  NOT not_3 (.in_1(cmp1_1_out_4), .out_2(a_b_2));
endmodule

module CMP1 (
  input  in_1,
  input  in_2,
  output out_3,
  output out_4
);

  and a_b (out_3, ~in_1, in_2);  // AND_Gate
  or a__b (out_4, ~in_1, in_2);  // OR_Gate
endmodule

module NOT (
  input  in_1,
  output out_2
);

  wire cmp1_1_out_4;

  CMP1 cmp1_1 (.in_1(in_1), .in_2(in_1), .out_4(cmp1_1_out_4));  // open: out_3
  CMP1 cmp1_2 (.in_1(in_1), .out_3(out_2), .in_2(cmp1_1_out_4));  // open: out_4
endmodule

module EQ1 (
  input  in_1,
  input  in_2,
  output out_3
);

  wire cmp1_1_out_3, cmp1_1_out_4;

  CMP1 cmp1_1 (.in_1(in_1), .out_3(cmp1_1_out_3), .in_2(in_2), .out_4(cmp1_1_out_4));
  CMP1 cmp1_2 (.in_1(cmp1_1_out_3), .out_3(out_3), .in_2(cmp1_1_out_4));  // open: out_4
endmodule
