// Logisim project ALU.circ as structural Verilog: 8 circuits, main circuit main
module main (
  input  [3:0] a3a2a1a0,
  input  [3:0] b3b2b1b0,
  input  [2:0] opcode,
  output c4,
  output [3:0] s3s2s1s0
);

  ALU4 alu4_1 (.c4(c4), .a3a2a1a0(a3a2a1a0), .b3b2b1b0(b3b2b1b0), .s3s2s1s0(s3s2s1s0), .opcode(opcode));

  // Notes on the sheet:
  //   000 et bit-à-bit
  //   001 not a
  //   010 ou bit-à-bit
  //   011 xor bit-à-bit
  //   1** addition
  //   1** addition
endmodule

module ADD1 (
  input  a,
  input  b,
  input  c0,
  output c1,
  output s
);

  wire and_1_out, and_2_out, xor_1_out;

  or or_1 (c1, and_1_out, and_2_out);
  and and_1 (and_1_out, a, b);
  xor xor_1 (xor_1_out, a, b);
  and and_2 (and_2_out, xor_1_out, c0);
  xor xor_2 (s, xor_1_out, c0);
endmodule

module ADD4 (
  input  [3:0] a3a2a1a0,
  input  [3:0] b3b2b1b0,
  output c4,
  output [3:0] s3s2s1s0
);

  wire add1_2_c1, add1_3_c1, add1_4_c1;

  ADD1 add1_1 (.c1(c4), .a(a3a2a1a0[3]), .b(b3b2b1b0[3]), .s(s3s2s1s0[3]), .c0(add1_3_c1));
  ADD1 add1_2 (.c1(add1_2_c1), .a(a3a2a1a0[1]), .b(b3b2b1b0[1]), .s(s3s2s1s0[1]), .c0(add1_4_c1));
  ADD1 add1_3 (.c1(add1_3_c1), .a(a3a2a1a0[2]), .b(b3b2b1b0[2]), .s(s3s2s1s0[2]), .c0(add1_2_c1));
  ADD1 add1_4 (.c1(add1_4_c1), .a(b3b2b1b0[0]), .b(a3a2a1a0[0]), .s(s3s2s1s0[0]), .c0(1'b0));
endmodule

module SUB4 (
);


  // Notes on the sheet:
  //   module SUB4 volontairement vide
  //   pour une opération soustracteur
  //   il faut adapter ADD4 avec une commande 1bit
endmodule

module INC4 (
  input  [3:0] Bin,
  output [3:0] Bin_1
);

  wire and_1_out, and_2_out;

  xor xor_1 (Bin_1[3], Bin[3], and_1_out);
  and and_1 (and_1_out, Bin[2], and_2_out);
  xor xor_2 (Bin_1[2], Bin[2], and_2_out);
  and and_2 (and_2_out, Bin[1], Bin[0]);
  xor xor_3 (Bin_1[1], Bin[1], Bin[0]);
  not not_1 (Bin_1[0], Bin[0]);
endmodule

module DEC3 (
  input  [2:0] a2a1a0,
  output [7:0] seul_le_bit_en_position__a2a1a0__2_vaut_1
);

  and s7 (seul_le_bit_en_position__a2a1a0__2_vaut_1[7], a2a1a0[2], a2a1a0[1], a2a1a0[0]);
  and s5 (seul_le_bit_en_position__a2a1a0__2_vaut_1[5], a2a1a0[2], ~a2a1a0[1], a2a1a0[0]);  // AND_Gate
  and s6 (seul_le_bit_en_position__a2a1a0__2_vaut_1[6], a2a1a0[2], a2a1a0[1], ~a2a1a0[0]);  // AND_Gate
  and s4 (seul_le_bit_en_position__a2a1a0__2_vaut_1[4], a2a1a0[2], ~a2a1a0[1], ~a2a1a0[0]);  // AND_Gate
  and s3 (seul_le_bit_en_position__a2a1a0__2_vaut_1[3], ~a2a1a0[2], a2a1a0[1], a2a1a0[0]);  // AND_Gate
  and s2 (seul_le_bit_en_position__a2a1a0__2_vaut_1[2], ~a2a1a0[2], a2a1a0[1], ~a2a1a0[0]);  // AND_Gate
  and s1 (seul_le_bit_en_position__a2a1a0__2_vaut_1[1], ~a2a1a0[2], ~a2a1a0[1], a2a1a0[0]);  // AND_Gate
  and s0 (seul_le_bit_en_position__a2a1a0__2_vaut_1[0], ~a2a1a0[2], ~a2a1a0[1], ~a2a1a0[0]);  // AND_Gate

  // Notes on the sheet:
  //   dec3: décodeur 3 bits (classique: position 0 à droite)
endmodule

module ALU4 (
  input  [3:0] a3a2a1a0,
  input  [3:0] b3b2b1b0,
  input  [2:0] opcode,
  output c4,
  output [3:0] s3s2s1s0
);

  wire [3:0] add4_1_s3s2s1s0, and_1_out, not_1_out, or_1_out, xor_1_out;

  ADD4 add4_1 (.a3a2a1a0(a3a2a1a0), .b3b2b1b0(b3b2b1b0), .c4(c4), .s3s2s1s0(add4_1_s3s2s1s0));
  assign xor_1_out = a3a2a1a0 ^ b3b2b1b0;  // XOR_Gate xor_1, 4 bits wide
  assign not_1_out = ~a3a2a1a0;  // NOT_Gate not_1, 4 bits wide
  assign and_1_out = a3a2a1a0 & b3b2b1b0;  // AND_Gate and_1, 4 bits wide
  assign or_1_out = a3a2a1a0 | b3b2b1b0;  // OR_Gate or_1, 4 bits wide
  PLX3 plx3_1 (
    .e4(add4_1_s3s2s1s0), .e5(add4_1_s3s2s1s0), .e6(add4_1_s3s2s1s0), .e7(add4_1_s3s2s1s0), .e3(xor_1_out),
    .e0(and_1_out), .e2(or_1_out), .e1(not_1_out), .\l_entrée__a2a1a0 (s3s2s1s0), .a2a1a0(opcode));
endmodule

module PLX3 (
  input  [3:0] e4,
  input  [3:0] e3,
  input  [3:0] e0,
  input  [3:0] e5,
  input  [3:0] e2,
  input  [3:0] e6,
  input  [3:0] e1,
  input  [3:0] e7,
  input  [2:0] a2a1a0,
  output [3:0] \l_entrée__a2a1a0 
);

  wire [3:0] s0_out, s1_out, s2_out, s3_out, s4_out, s5_out, s6_out, s7_out;

  assign s7_out = {4{a2a1a0[2]}} & {4{a2a1a0[1]}} & {4{a2a1a0[0]}} & e7;  // AND_Gate s7, 4 bits wide
  assign s6_out = {4{a2a1a0[2]}} & {4{a2a1a0[1]}} & ~{4{a2a1a0[0]}} & e6;  // AND_Gate s6, 4 bits wide
  assign s5_out = {4{a2a1a0[2]}} & ~{4{a2a1a0[1]}} & {4{a2a1a0[0]}} & e5;  // AND_Gate s5, 4 bits wide
  assign s4_out = {4{a2a1a0[2]}} & ~{4{a2a1a0[1]}} & ~{4{a2a1a0[0]}} & e4;  // AND_Gate s4, 4 bits wide
  assign s2_out = ~{4{a2a1a0[2]}} & {4{a2a1a0[1]}} & ~{4{a2a1a0[0]}} & e2;  // AND_Gate s2, 4 bits wide
  assign s3_out = ~{4{a2a1a0[2]}} & {4{a2a1a0[1]}} & {4{a2a1a0[0]}} & e3;  // AND_Gate s3, 4 bits wide
  assign \l_entrée__a2a1a0  = s7_out | s6_out | s5_out | s4_out | s3_out | s2_out | s1_out | s0_out;  // OR_Gate or_1, 4 bits wide
  assign s1_out = ~{4{a2a1a0[2]}} & ~{4{a2a1a0[1]}} & {4{a2a1a0[0]}} & e1;  // AND_Gate s1, 4 bits wide
  assign s0_out = ~{4{a2a1a0[2]}} & ~{4{a2a1a0[1]}} & ~{4{a2a1a0[0]}} & e0;  // AND_Gate s0, 4 bits wide
endmodule
